// Logisim project AHB-Lite (Single Master).circ as structural Verilog: 1 circuit, main circuit main
module main (
  input  [7:0] HADDR,
  input  HREADY,
  input  [7:0] HWDATA,
  input  HWRITE,
  input  CLK,
  output [7:0] HRDATA
);

  wire not_1_out, register_2_q;
  wire [7:0] register_1_q;

  Register register_1 (.D(HADDR), .en(HREADY), .Q(register_1_q), .clk(CLK));  // open: clr
  Register #(.width(1)) register_2 (.D(HWRITE), .en(HREADY), .Q(register_2_q), .clk(CLK));  // open: clr
  not not_1 (not_1_out, register_2_q);
  RAM #(.bus("separate")) ram_1 (
    .addr(register_1_q), .din(HWDATA), .data(HRDATA), .str(register_2_q), .sel(1'b1), .clk(CLK),
    .ld(not_1_out));  // open: clr
endmodule
